# Fritzing sketch arduinoproto (saved by Fritzing 0.9.3b)
circuit board: 3.65403cm x 3.15656cm
breadboards: 2

parts:
  328 = ATmega328 [package=tqfp]
  clock1 = Resonator [package=resonator-smd]
  C9 = Ceramic Capacitor [capacitance=0.1µF package="0805 [SMD, multilayer]"]
  R6 = Resistor [tolerance=±5% resistance=10k package="0805 [SMD]"]
  prog = Header 6 [package=em406]
  rst = SWITCH-MOMENTARY-2 [package=tactile-switch-1101ne]
  max485 = RS485 [package=so08]
  U2 = RJ45 Jack [package=rj45-8]
  U3 = RJ45 Jack [package=rj45-8]
  C10 = Ceramic Capacitor [capacitance=0.1µF package="0805 [SMD, multilayer]"]
  i2c = female pin header, 2 pins [form="♀ (female)"]
  D5-D10 = female pin header, 6 pins [form="♀ (female)"]
  MOSI = female pin header, 1 pin [form="♀ (female)"]
  MISO = female pin header, 1 pin [form="♀ (female)"]
  A0-A3 = female pin header, 4 pins [form="♀ (female)"]

nets:
  N1: 328.PD3(INT1), max485.DI
  N2: 328.PD4(XCK_T0), max485.DE
  GND: 328.GND, 328.AGND, clock1.2, prog.1, prog.2, rst.2, max485._RE, max485.GND, U2.1, U3.1, C10.1
  VCC: 328.VCC, 328.AVCC, R6.Pin_1, prog.3, max485.VCC, U2.2, U3.2, C10.0
  N3: 328.PB6(XTAL1_TOSC1), clock1.1
  N4: 328.PB7(XTAL2_TOSC2), clock1.3
  N5: 328.PD5(T1), D5-D10.pin1
  N6: 328.PD6(AIN0), D5-D10.pin2
  N7: 328.PD7(AIN1), D5-D10.pin3
  N8: 328.PB0(ICP), D5-D10.pin4
  N9: 328.PB1(OC1A), D5-D10.pin5
  N10: 328.PB2(SS_OC1B), D5-D10.pin6
  N11: 328.PB3(MOSI_OC2), MOSI.pin1
  N12: 328.PB4(MISO), MISO.pin1
  N13: 328.PC0(ADC0), A0-A3.pin4
  N14: 328.PC1(ADC1), A0-A3.pin3
  N15: 328.PC2(ADC2), A0-A3.pin2
  N16: 328.PC3(ADC3), A0-A3.pin1
  N17: 328.PC4(ADC4_SDA), i2c.pin2
  N18: 328.PC5(ADC5_SCL), i2c.pin1
  N19: 328.PC6(_RESET), C9.1, R6.Pin_0, rst.1
  N20: 328.PD0(RXD), prog.4
  N21: 328.PD1(TXD), prog.5
  N22: 328.PD2(INT0), max485.RO
  N23: C9.0, prog.6
  N24: max485.A, U2.3, U3.3
  N25: max485.B, U2.4, U3.4
