# Fritzing sketch relaysketch (saved by Fritzing 0.9.3b)
circuit board: 3.59148cm x 4.00453cm
breadboards: 1

parts:
  Q1 = NPN-Transistor [package="SOT-23 [SMD]"]
  bus = RJ45 Jack [package=rj45-8]
  bus_2 = RJ45 Jack [package=rj45-8]
  load = Header 2 [package=jst-2-pth]
  1117 = Voltage Regulator LM1117 [package=sot223]
  Q2 = NPN-Transistor [package="SOT-23 [SMD]"]
  D1 = Diode [package=sod-323]
  R1 = Resistor [tolerance=±5% resistance=220 package="0805 [SMD]"]
  R2 = Resistor [tolerance=±5% resistance=220 package="0805 [SMD]"]
  led1 = ws2812b [package="smd 2812b"]
  led2 = ws2812b [package="smd 2812b"]
  led3 = ws2812b [package="smd 2812b"]
  on = smd LED [color="Red (633nm)" package="0805 [SMD]"]
  rev = smd LED [color="Red (633nm)" package="0805 [SMD]"]
  R3 = Resistor [tolerance=±5% resistance=220 package="0805 [SMD]"]
  R4 = Resistor [tolerance=±5% resistance=220 package="0805 [SMD]"]
  ACS712 = MOSFET-NCHANNEL-SOIC8 [package=so08]
  J2 = female pin header, 2 pins [form="♀ (female)"]
  J3 = female pin header, 7 pins [form="♀ (female)"]
  term = Resistor [tolerance=±5% resistance=220 package="0805 [SMD]"]
  Pad1 = Pad [width=1.1673088758167653 height=2.1951588158494459 connect=center]
  Pad2 = Pad [width=1.1673088758167653 height=2.1951588158494459 connect=center]
  DS2Y-5-DC5V3 = DS2Y-5-DC5V [part_number=DS2Y-5-DC5V]
  C1 = Ceramic Capacitor [capacitance=100nF package="0805 [SMD, multilayer]"]
  C2 = Ceramic Capacitor [capacitance=100nF package="0805 [SMD, multilayer]"]

nets:
  VDD: Q1.2, bus.2, bus_2.2, 1117.OUT, Q2.2, D1.C, led1.VDD, led1.VSS, led2.VDD, led2.VSS, led3.VDD, led3.VSS, R3.Pin_0, R4.Pin_1, ACS712.D, J2.pin1, J2.pin2, J3.pin3, J3.pin5, DS2Y-5-DC5V3.1_+, C1.1
  N1: Q1.0, R1.Pin_0
  N2: Q1.1, DS2Y-5-DC5V3.6_N.C., DS2Y-5-DC5V3.9_N.O.
  N3: bus.1, bus_2.1, 1117.IN, ACS712.S, ACS712.G, DS2Y-5-DC5V3.8_N.O., DS2Y-5-DC5V3.11_N.C., C2.0
  N4: bus.3, bus_2.3, J3.pin7, term.Pin_1
  N5: bus.4, bus_2.4, J3.pin6, term.Pin_0
  N6: load.1, Pad1.pad, DS2Y-5-DC5V3.4_COM
  N7: load.2, Pad2.pad, DS2Y-5-DC5V3.13_COM
  N8: 1117.ADJ, C1.0, C2.1
  N9: Q2.0, R2.Pin_0
  N10: Q2.1, D1.A, DS2Y-5-DC5V3.16_-
  N11: R1.Pin_1, on.anode
  N12: R2.Pin_1, rev.anode
  N13: led1.DOUT, led2.DIN
  N14: led1.DIN, led3.DOUT
  N15: led3.DIN, J3.pin4
  N16: on.cathode, R3.Pin_1, J3.pin1
  N17: rev.cathode, R4.Pin_0, J3.pin2

notes:
  gnd
  5v
  npx
  A
  B
  ocf
  lss
  on
  rev

custom parts:
  DS2Y-5-DC5V: Panasonic DS2Y-5-DC5V Relay with 2 form C contact
